# Fritzing sketch arduinoFTDI (saved by Fritzing 0.9.3b)

parts:
  Composant1 = Arduino Uno (Rev3)
  VCC1 = Battery

nets:
  N1: Composant1.RESET, Composant1.GND, VCC1.+
  N2: Composant1.VIN, VCC1.-

notes:
  vers RX
  vers TX
